# Fritzing sketch fritzing-parallel (saved by Fritzing 0.9.3b)
circuit board: 8.46667cm x 5.64444cm
breadboards: 1

parts:
  U1 = NodeMCU V1.0
  Componente1 = DB25F
  U2 = 74HC595 [package="DIP16 [THT]"]

nets:
  N1: U1.D2, U2.DS
  N2: U1.D3, U2.ST_CP
  N3: U1.D4, U2.SH_CP
  3V3: U1.3V3, U2.MR, U2.VCC
  GND: U1.GND, Componente1.pin18, Componente1.pin19, Componente1.pin20, Componente1.pin21, Componente1.pin22, Componente1.pin23, Componente1.pin24, Componente1.pin25, U2.GND, U2.OE
  N4: U1.D5, Componente1.pin11
  N5: U1.D6, Componente1.pin1
  N6: Componente1.pin2, U2.Q0
  N7: Componente1.pin3, U2.Q1
  N8: Componente1.pin4, U2.Q2
  N9: Componente1.pin5, U2.Q3
  N10: Componente1.pin6, U2.Q4
  N11: Componente1.pin7, U2.Q5
  N12: Componente1.pin8, U2.Q6
  N13: Componente1.pin9, U2.Q7

custom parts:
  NodeMCU V1.0: ESP8266 based NodeMCU
