# Fritzing sketch fritzing-usb-ch375 (saved by Fritzing 0.9.3b)
breadboards: 1

parts:
  U1 = NodeMCU V1.0
  R1 = Resistor [tolerance=±5% resistance=1k package=THT]
  Q2 = NPN-Transistor [part_number=2N2222 package="TO92 [THT]"]
  R2 = Resistor [tolerance=±5% resistance=1k package=THT]
  R3 = Resistor [tolerance=±5% resistance=1k package=THT]
  R4 = Resistor [tolerance=±5% resistance=1k package=THT]
  Q1 = NPN-Transistor [part_number=2N2222 package="TO92 [THT]"]
  Componente1 = CH375

nets:
  N1: U1.D3, R1.Pin_0
  N2: U1.D4, Componente1.INT
  GND: U1.GND, Q2.E, Q1.E, Componente1.GND
  N3: U1.D6, Componente1.unknown#22
  VIN: U1.Vin, R3.Pin_1, R4.Pin_1, Componente1.VCC
  N4: R1.Pin_1, Q1.B
  N5: Q2.B, R2.Pin_1
  N6: Q2.C, R4.Pin_0, Componente1.S
  N7: R2.Pin_0, R3.Pin_0, Q1.C
  N8: Componente1.unknown#19, Componente1.unknown#20

custom parts:
  NodeMCU V1.0: ESP8266 based NodeMCU
